# Fritzing sketch circuit (saved by Fritzing 0.9.3b)
breadboards: 1

parts:
  BT1 = Bluetooth HC-06u [package=THT]
  J1 = Piezo Speaker
  J2 = Basic Servo
  부품1 = Arduino Uno (Rev3)

nets:
  VCC: BT1.VCC, J1.pin1, J2.vcc, 부품1.5V
  GND: BT1.GND, J2.gnd, 부품1.GND
  N1: BT1.TXD, 부품1.D0/RX
  N2: BT1.RXD, 부품1.D1/TX
  N3: J1.pin2, 부품1.D2
  N4: J2.pulse, 부품1.D8

custom parts:
  Bluetooth HC-06u: Bluetooth HC-06 - face up, pins down 16.5mm x 37.5mm PCB
